# Fritzing sketch schematic (saved by Fritzing 0.9.1b)
breadboards: 1

parts:
  Part1 = Arduino Uno (Rev3)
  U1 = ESP8266 WiFi Module [part_number=ESP8266]
  IC1 = Voltage Regulator [package=to-92]
  V1 = DC Power [voltage=5]
  M1 = DC Motor
  M2 = DC Motor
  Part3 = Logic Level Converter
  Part2 = L9110S Dual Motor Driver

nets:
  N1: Part1.D8, Part2.B-IA
  N2: Part1.D9_PWM, Part2.B-IB
  N3: Part1.D10_PWM/SS, Part2.A-IA
  N4: Part1.D11_PWM/MOSI, Part2.A-IB
  GND: Part1.GND, U1.GND, IC1.GND, V1.V-, Part3.GND, Part2.GND
  N5: Part1.D2, Part3.TX_HV
  N6: Part1.D3_PWM, Part3.RX_LV
  N7: Part1.VIN, IC1.IN, V1.V+, Part3.HV
  N8: U1.RXD, Part3.RX_HV
  VCC: U1.VCC, IC1.OUT, Part3.LV, Part2.VCC
  N9: U1.TXD, Part3.TX_LV
  N10: M1.pin_1, Part2.B-OB
  N11: M1.pin_2, Part2.B-OA
  N12: M2.pin_1, Part2.A-OB
  N13: M2.pin_2, Part2.A-OA

custom parts:
  ESP8266 WiFi Module: Generic WiFi Module based on the ESP8266 with onboard PCB antenna and UART communications
